# Fritzing sketch BreadPlayer (saved by Fritzing 1.0.6)
circuit board: 30.5244cm x 15.257cm
breadboards: 1

parts:
  U3 = ESP32-38PinWide [part_number=ESP32-38PinWide]
  Waveshare_e-Ink_Paper_Display_with_SPI_Interface = Waveshare e-Paper HAT [package=THT]
  LiPo_Battery_3_7V = Lithium Ion Polymer Battery 3.7v 950mAh
  PCM5102a = Pcm5102A module
  3_5mm_TRS_Jack = SUYIN Audio Jack (TRS) 3.5mm [package="SUYIN [THT]"]
  MicroSD_SPI_Module = microSD Card Module
  Tactile_Buttons = SWITCH-MOMENTARY-2 [package=tactile-pth]
  S8 = SWITCH-MOMENTARY-2 [package=tactile-pth]
  S6 = SWITCH-MOMENTARY-2 [package=tactile-pth]
  TP4056_Charger_Module = TP4056 Module [part_number=HW-107]
  U2 = SWITCH-SPST-2 [package=switch-spst-vertical]
  M2 = bb-usb-cable [package=THT]  # not connected
  MT3608 = MT3608 Boost No usb

nets:
  N1: U3.3.3, Waveshare_e-Ink_Paper_Display_with_SPI_Interface.pin_8, PCM5102a.Pin_6, MicroSD_SPI_Module.3.3V
  N2: U3.GPIO32, PCM5102a.Pin_4
  N3: U3.GPIO33, PCM5102a.Pin_3
  N4: U3.GPIO25, Waveshare_e-Ink_Paper_Display_with_SPI_Interface.pin_1
  N5: U3.GPIO26, Waveshare_e-Ink_Paper_Display_with_SPI_Interface.pin_2
  N6: U3.GPIO27, Waveshare_e-Ink_Paper_Display_with_SPI_Interface.pin_3
  N7: U3.GPIO14, Waveshare_e-Ink_Paper_Display_with_SPI_Interface.pin_6
  GND: U3.GND, MicroSD_SPI_Module.GND, Tactile_Buttons.1, S8.1, S6.1, TP4056_Charger_Module.OUT-#1, MT3608.IN_(-), MT3608.OUT_(-)
  N8: U3.GPIO13, Waveshare_e-Ink_Paper_Display_with_SPI_Interface.pin_5
  N9: U3.GPIO11, Waveshare_e-Ink_Paper_Display_with_SPI_Interface.pin_7, PCM5102a.Pin_1, PCM5102a.Pin_5
  N10: U3.VIN, U2.O, MT3608.IN_(+)
  N11: U3.GPIO15, Waveshare_e-Ink_Paper_Display_with_SPI_Interface.pin_4
  N12: U3.GPIO4, MicroSD_SPI_Module.CS
  N13: U3.GPIO16, S6.2
  N14: U3.GPIO17, Tactile_Buttons.2
  N15: U3.GPIO5, MicroSD_SPI_Module.CLK
  N16: U3.GPIO18, PCM5102a.Pin_2
  N17: U3.GPIO19, MicroSD_SPI_Module.MISO
  N18: U3.GPIO21, S8.2
  N19: U3.GPIO23, MicroSD_SPI_Module.MOSI
  N20: LiPo_Battery_3_7V.positive, TP4056_Charger_Module.BAT+
  N21: LiPo_Battery_3_7V.negative, TP4056_Charger_Module.BAT-
  N22: PCM5102a.Pin_7, 3_5mm_TRS_Jack.Tip
  N23: PCM5102a.Pin_8, PCM5102a.Pin_10, 3_5mm_TRS_Jack.Sleeve
  N24: PCM5102a.Pin_9, 3_5mm_TRS_Jack.Ring
  N25: TP4056_Charger_Module.OUT-#4, U2.P

custom parts:
  ESP32-38PinWide: Generic 38-Pin ESP32 with wide format (only access to one side of pins on a breadboard) based on Stephen Lilley's HiLetgo ESP-WROOM-32 ESP32 ESP-32S Development Board.
  Waveshare e-Paper HAT: .This is a universal driver board for e-Paper raw panels, can be used to drive various SPI interface e-Paper from Waveshare.
  Lithium Ion Polymer Battery 3.7v 950mAh: Lithium ion polymer (also known as 'lipo' or 'lipoly') batteries are thin, light and powerful. The output ranges from 4.2V when completely charged to 3.7V. This battery has a capacity of 950mAh. The batteries include the necessary protection circuitry.
  Pcm5102A module: Interface I2S PCM5102A DAC Decoder GY-PCM5102 I2S Player Module for Raspberry Pi pHAT Format Board Digital PCM5102 Audio Board.
  SUYIN Audio Jack (TRS) 3.5mm: Stereo Jack 3.5mm
  microSD Card Module: microSD Card Reader This is a simple, generic, 3.3V only SD card reader module. It does not include any regulator or logic level shifting circuitry.
  TP4056 Module: TP4056 Lithium Battery Charge Management Module Links: TP4056 website
  bb-usb-cable: Breadboard only, no connectors USB cable for the Raspberry PIs.
  MT3608 Boost No usb: Chip- MT3608 / B6289 DC to DC step up, power booster module. With adjustable output voltage. Current- 2A . || Input voltage- 2V-24V || Output voltage- 5V-28V Input interface- Inversed polarity- NO. || Led indicator- No.
