# Fritzing sketch switch01 (saved by Fritzing 0.9.3b)
breadboards: 1

parts:
  S1 = Pushbutton [package="[THT]"]
  S2 = Pushbutton [package="[THT]"]
  S3 = Pushbutton [package="[THT]"]
  S4 = Pushbutton [package="[THT]"]
  S5 = Pushbutton [package="[THT]"]
  パーツ1 = Arduino Mega 2560 (Rev3)

nets:
  N1: S1.Pin_1, S1.Pin_2, パーツ1.D21/SCL
  N2: S1.Pin_3, S1.Pin_4, S2.Pin_3, S2.Pin_4, S3.Pin_3, S3.Pin_4, S4.Pin_3, S4.Pin_4, S5.Pin_3, S5.Pin_4, パーツ1.GND
  N3: S2.Pin_1, S2.Pin_2, パーツ1.D5_PWM
  N4: S3.Pin_1, S3.Pin_2, パーツ1.D17_PWM/RX2
  N5: S4.Pin_1, S4.Pin_2, S5.Pin_1, S5.Pin_2, パーツ1.D18/TX1
